# Fritzing sketch ubox_head_controller (saved by Fritzing 0.9.2b)
circuit board: 6cm x 5.3cm
breadboards: 1

parts:
  ULN2803A = ULN2803A [package=THT]
  M1 = female pin header, 5 pins [form="♀ (female)"]
  Crystal = Crystal [frequency="16 Mhz" package=THT]
  LDR = Photocell (LDR) [package=THT]
  R3 = Resistor [tolerance=±5% resistance=220 package=THT]
  US-020 = female pin header, 4 pins [form="♀ (female)"]
  Piezo = Piezo Speaker  # not connected
  ICSP = Generic ICSP header - 6 pins [form="♂ (male)" package=THT]  # not connected
  Atmega = atmega328 [package=dip]
  M2 = female pin header, 5 pins [form="♀ (female)"]
  Webcam = male pin header, 4 pins [form="♂ (male)"]
  R1 = Resistor [tolerance=±5% resistance=10k power=5 package=THT]
  5V = Battery
  COMs = female pin header, 2 pins [form="♀ (female)" part_number=TX.RX]
  Q1 = NPN-Transistor [package="TO92 [THT]"]
  LZ = female pin header, 2 pins [form="♀ (female)" part_number=Lazer]
  TR2 = TRIMPOT [part_number=TRLaser package=trim_pot_pth]
  R4 = Resistor [tolerance=±5% resistance=10k power=5 package=THT]
  C2 = Tantalum Capacitor [capacitance=22pF package="100 mil [THT, tantalum]"]
  C3 = Tantalum Capacitor [capacitance=22pF package="100 mil [THT, tantalum]"]
  C1 = Tantalum Capacitor [capacitance=1μF package="100 mil [THT, tantalum]"]
  5-12v = Battery
  JMP1 = male pin header, 2 pins [form="♂ (male)"]
  JMP2 = male pin header, 2 pins [form="♂ (male)"]
  TR1 = TRIMPOT [package=trim_pot_pth]  # not connected
  RST = Pushbutton [package="[THT]"]
  LED = LED - 3mm [color="Red (633nm)" package="3 mm [THT]"]

nets (from the pcb view):
  N1: ULN2803A.0V, C1.-, 5-12v.-, JMP2.pin2
  N2: ULN2803A.COM_-_Common, M1.pin5, M2.pin5, C1.+, 5-12v.+, JMP1.pin1
  N3: ULN2803A.Out_8, M2.pin4
  N4: ULN2803A.Out_7, M2.pin3
  N5: ULN2803A.Out_6, M2.pin2
  N6: ULN2803A.Out_5, M2.pin1
  N7: ULN2803A.Out_4, M1.pin4
  N8: ULN2803A.Out_3, M1.pin3
  N9: ULN2803A.Out_2, M1.pin2
  N10: ULN2803A.Out_1, M1.pin1
  N11: Crystal.pin_0, Atmega.XLAT1, C3.-
  N12: Crystal.pin_1, Atmega.XLAT2, C2.-
  N13: LDR.pin_0, US-020.pin4, Atmega.VCC, Atmega.AVCC, Webcam.pin1, R1.Pin_0, 5V.+, Q1.C, JMP1.pin2
  N14: LDR.pin_1, Atmega.A5, R4.Pin_0
  N15: R3.Pin_0, US-020.pin1, Atmega.GND, Webcam.pin2, 5V.-, LZ.pin1, TR2.CW, R4.Pin_1, C2.+, C3.+, JMP2.pin1, RST.Pin_1, RST.Pin_2
  N16: R3.Pin_1, LED.cathode
  N17: US-020.pin2, Atmega.D4
  N18: US-020.pin3, Atmega.D3_(PWM)
  N19: Atmega.RESET, R1.Pin_1, RST.Pin_3, RST.Pin_4
  N20: Atmega.D0_(RX), COMs.pin2
  N21: Atmega.D1_(TX), COMs.pin1
  N22: Atmega.D13, TR2.CCW, LED.anode
  N23: Q1.E, LZ.pin2
  N24: Q1.B, TR2.WIPER
