# Fritzing sketch ubox_head_controller_bkp11 (saved by Fritzing 0.9.2b)
circuit board: 6cm x 5.3cm
breadboards: 1

parts:
  ULN2803A = ULN2803A [package=THT]
  M1 = female pin header, 5 pins [form="♀ (female)"]
  Crystal = Crystal [frequency="16 Mhz" package=THT]
  LDR = Photocell (LDR) [package=THT]
  R3 = Resistor [tolerance=±5% resistance=220 package=THT]
  US-020 = female pin header, 4 pins [form="♀ (female)"]
  Piezo = Piezo Speaker
  ICSP = Generic ICSP header - 6 pins [form="♂ (male)" package=THT]
  Atmega = atmega328 [package=dip]
  M2 = female pin header, 5 pins [form="♀ (female)"]
  Webcam = male pin header, 4 pins [form="♂ (male)"]
  R1 = Resistor [tolerance=±5% resistance=10k power=5 package=THT]
  5V = Battery
  COMs = female pin header, 2 pins [form="♀ (female)" part_number=TX.RX]
  Q1 = NPN-Transistor [package="TO92 [THT]"]
  LZ = female pin header, 2 pins [form="♀ (female)" part_number=Lazer]
  TR2 = TRIMPOT [part_number=TRLaser package=trim_pot_pth]
  R4 = Resistor [tolerance=±5% resistance=10k power=5 package=THT]
  C2 = Tantalum Capacitor [capacitance=22pF package="100 mil [THT, tantalum]"]
  C3 = Tantalum Capacitor [capacitance=22pF package="100 mil [THT, tantalum]"]
  C1 = Tantalum Capacitor [capacitance=1μF package="100 mil [THT, tantalum]"]
  5-12v = Battery
  JMP1 = male pin header, 2 pins [form="♂ (male)"]
  JMP2 = male pin header, 2 pins [form="♂ (male)"]
  TR1 = TRIMPOT [package=trim_pot_pth]
  RST = Pushbutton [package="[THT]"]
  LED = LED - 3mm [color="Red (633nm)" package="3 mm [THT]"]

nets (from the breadboard view):
  N1: ULN2803A.In_1, Atmega.D4
  N2: ULN2803A.In_2, Atmega.D5_(PWM)
  N3: ULN2803A.In_3, Atmega.D6_(PWM)
  N4: ULN2803A.In_4, Atmega.D7
  N5: ULN2803A.In_5, Atmega.D8
  N6: ULN2803A.In_6, Atmega.D9_(PWM)
  N7: ULN2803A.In_7, Atmega.D10_(PWM)
  N8: ULN2803A.In_8, ICSP.pin4, Atmega.D11_(PWM)
  N9: ULN2803A.0V, R3.Pin_1, US-020.pin1, Piezo.pin1, ICSP.pin6, Atmega.GND, Webcam.pin1, 5V.-, LZ.pin1, TR2.CW, R4.Pin_1, C2.-, C3.+, C1.-, 5-12v.-, JMP2.pin1, JMP2.pin2, TR1.CW, RST.Pin_3, RST.Pin_4
  N10: ULN2803A.COM_-_Common, M1.pin5, ICSP.pin2, Atmega.VCC, M2.pin5, R1.Pin_0, C1.+, 5-12v.+, JMP1.pin1, JMP1.pin2
  N11: ULN2803A.Out_8, M2.pin4
  N12: ULN2803A.Out_7, M2.pin3
  N13: ULN2803A.Out_6, M2.pin2
  N14: ULN2803A.Out_5, M2.pin1
  N15: ULN2803A.Out_4, M1.pin4
  N16: ULN2803A.Out_3, M1.pin3
  N17: ULN2803A.Out_2, M1.pin2
  N18: ULN2803A.Out_1, M1.pin1
  N19: Crystal.pin_0, Atmega.XLAT1, C2.+
  N20: Crystal.pin_1, Atmega.XLAT2, C3.-
  N21: LDR.pin_0, US-020.pin4, Atmega.AVCC, Webcam.pin4, 5V.+, Q1.C
  N22: LDR.pin_1, Atmega.A5, R4.Pin_0
  N23: R3.Pin_0, LED.cathode
  N24: US-020.pin2, ICSP.pin1, Atmega.D12
  N25: US-020.pin3, Atmega.D3_(PWM)
  N26: Piezo.pin2, TR1.WIPER
  N27: ICSP.pin3, Atmega.D13, TR2.CCW, LED.anode
  N28: ICSP.pin5, Atmega.RESET, R1.Pin_1, RST.Pin_1, RST.Pin_2
  N29: Atmega.D0_(RX), COMs.pin2
  N30: Atmega.D1_(TX), COMs.pin1
  N31: Atmega.D2, TR1.CCW
  N32: Q1.E, LZ.pin2
  N33: Q1.B, TR2.WIPER
