# Fritzing sketch ubox_head_controller_bkp6 (saved by Fritzing 0.9.2b)
breadboards: 1

parts:
  ULN2803A = ULN2803A [package=THT]
  M1 = female pin header, 5 pins [form="♀ (female)"]
  Crystal = Crystal [frequency="16 Mhz" package=THT]
  LDR = Photocell (LDR) [package=THT]
  S1 = Pushbutton [package="[THT]"]
  R3 = Resistor [tolerance=±5% resistance=220 package=THT]
  US-020 = female pin header, 4 pins [form="♀ (female)"]
  Piezo = Piezo Speaker
  ICSP = Generic ICSP header - 6 pins [form="♂ (male)" package=THT]
  Atmega = atmega328 [package=dip]
  M2 = female pin header, 5 pins [form="♀ (female)"]
  Webcam = male pin header, 4 pins [form="♂ (male)"]
  C2 = Tantalum Capacitor [capacitance=22pF package="200 mil [THT, tantalum]"]
  C3 = Tantalum Capacitor [capacitance=22pF package="200 mil [THT, tantalum]"]
  C1 = Tantalum Capacitor [capacitance=1μF package="200 mil [THT, tantalum]"]
  R4 = Resistor [tolerance=±5% resistance=10k power=5 package=THT]
  LED1 = LED - 3mm [color="Red (633nm)" package="3 mm [THT]"]
  TR5 = TRIMPOT [package=trim_pot_pth]
  R1 = Resistor [tolerance=±5% resistance=10k power=5 package=THT]
  VCC1 = Battery
  TXRX = female pin header, 2 pins [form="♀ (female)"]
  Q1 = NPN-Transistor [package="TO92 [THT]"]
  LASER = female pin header, 2 pins [form="♀ (female)"]
  TR6 = TRIMPOT [package=trim_pot_pth]

nets:
  N1: ULN2803A.In_1, Atmega.D4
  N2: ULN2803A.In_2, Atmega.D5_(PWM)
  N3: ULN2803A.In_3, Atmega.D6_(PWM)
  N4: ULN2803A.In_4, Atmega.D7
  N5: ULN2803A.In_5, Atmega.D8
  N6: ULN2803A.In_6, Atmega.D9_(PWM)
  N7: ULN2803A.In_7, Atmega.D10_(PWM)
  N8: ULN2803A.In_8, ICSP.pin4, Atmega.D11_(PWM)
  N9: ULN2803A.0V, S1.Pin_3, S1.Pin_4, R3.Pin_1, US-020.pin1, Piezo.pin1, ICSP.pin6, Atmega.GND, Webcam.pin1, C2.-, C3.+, C1.-, R4.Pin_1, TR5.CW, VCC1.-, LASER.pin1, TR6.CW
  N10: ULN2803A.COM_-_Common, M1.pin5, LDR.pin_0, US-020.pin4, ICSP.pin2, Atmega.VCC, Atmega.AVCC, M2.pin5, Webcam.pin4, C1.+, R1.Pin_0, VCC1.+, Q1.C
  N11: ULN2803A.Out_8, M2.pin4
  N12: ULN2803A.Out_7, M2.pin3
  N13: ULN2803A.Out_6, M2.pin2
  N14: ULN2803A.Out_5, M2.pin1
  N15: ULN2803A.Out_4, M1.pin4
  N16: ULN2803A.Out_3, M1.pin3
  N17: ULN2803A.Out_2, M1.pin2
  N18: ULN2803A.Out_1, M1.pin1
  N19: Crystal.pin_0, Atmega.XLAT1, C2.+
  N20: Crystal.pin_1, Atmega.XLAT2, C3.-
  N21: LDR.pin_1, R4.Pin_0
  N22: S1.Pin_1, S1.Pin_2, ICSP.pin5, Atmega.RESET, R1.Pin_1
  N23: R3.Pin_0, LED1.cathode
  N24: US-020.pin2, ICSP.pin1, Atmega.D12
  N25: US-020.pin3, Atmega.D3_(PWM)
  N26: Piezo.pin2, TR5.WIPER
  N27: ICSP.pin3, Atmega.D13, LED1.anode, TR6.CCW
  N28: Atmega.D0_(RX), TXRX.pin2
  N29: Atmega.D1_(TX), TXRX.pin1
  N30: Atmega.D2, TR5.CCW
  N31: Q1.E, LASER.pin2
  N32: Q1.B, TR6.WIPER
